# Fritzing sketch arduino-puzzle-box (saved by Fritzing 0.9.2b)
breadboards: 1

parts:
  Part1 = Arduino Uno (Rev3)
  LED1 = LED - 5mm [color="Red (633nm)" package="5 mm [THT]"]
  LED2 = LED - 5mm [color="Red (633nm)" package="5 mm [THT]"]
  LED3 = LED - 5mm [color="Red (633nm)" package="5 mm [THT]"]
  LED4 = LED - 5mm [color="Red (633nm)" package="5 mm [THT]"]
  LED5 = LED - 5mm [color="Red (633nm)" package="5 mm [THT]"]
  S1 = Pushbutton [package="[THT]"]
  R1 = Photocell (LDR) [package=THT]
  R2 = Resistor [tolerance=±5% resistance=1k package=THT]
  R3 = Resistor [tolerance=±5% resistance=1k package=THT]
  R4 = Resistor [tolerance=±5% resistance=1k package=THT]
  R5 = Resistor [tolerance=±5% resistance=1k package=THT]
  R6 = Resistor [tolerance=±5% resistance=10k package=THT]
  R7 = Resistor [tolerance=±5% resistance=1k package=THT]
  R8 = Resistor [tolerance=±5% resistance=10k package=THT]

nets:
  N1: Part1.A0, R1.pin_0, R7.Pin_0
  N2: Part1.GND, LED1.cathode, LED2.cathode, LED3.cathode, LED4.cathode, LED5.cathode, R7.Pin_1, R8.Pin_0
  N3: Part1.D2, R6.Pin_0
  N4: Part1.D3_PWM, R5.Pin_0
  N5: Part1.D4, R4.Pin_0
  N6: Part1.D5_PWM, R3.Pin_0
  N7: Part1.D6_PWM, R2.Pin_0
  N8: Part1.D7, S1.Pin_1, S1.Pin_2, R8.Pin_1
  N9: Part1.5V, S1.Pin_3, S1.Pin_4, R1.pin_1
  N10: LED1.anode, R6.Pin_1
  N11: LED2.anode, R5.Pin_1
  N12: LED3.anode, R4.Pin_1
  N13: LED4.anode, R3.Pin_1
  N14: LED5.anode, R2.Pin_1
